// Logisim project Circuit.circ as structural Verilog: 10 circuits, main circuit main
module main (
  input  A0,
  input  A1,
  input  B0,
  input  A2,
  input  B1,
  input  A3,
  input  B2,
  input  A4,
  input  B3,
  input  A5,
  input  B4,
  input  A6,
  input  B5,
  input  A7,
  input  B6,
  input  B7
);

  wire and_1_out, and_2_out, BTNC_out, BTNL_out, BTNR_out, Clk_out, clock_1_out, controlunit_1_ea,
       controlunit_1_eb, controlunit_1_ep, controlunit_1_la, controlunit_1_lb, controlunit_1_psel,
       controlunit_1_rstp, doubledabble_1_hundreds0, doubledabble_1_hundreds1, doubledabble_1_hundreds2,
       doubledabble_1_hundreds3, doubledabble_1_ones0, doubledabble_1_ones1, doubledabble_1_ones2,
       doubledabble_1_ones3, doubledabble_1_tens0, doubledabble_1_tens1, doubledabble_1_tens2,
       doubledabble_1_tens3, doubledabble_1_tenthousands0, doubledabble_1_tenthousands1,
       doubledabble_1_tenthousands2, doubledabble_1_tenthousands3, doubledabble_1_thousands0,
       doubledabble_1_thousands1, doubledabble_1_thousands2, doubledabble_1_thousands3, multiplexer_7_out,
       multiplexer_9_out, nor_1_out, or_1_out, shiftrightreg_1_out_0, shiftrightreg_1_out_1,
       shiftrightreg_1_out_2, shiftrightreg_1_out_3, shiftrightreg_1_out_4, shiftrightreg_1_out_5,
       shiftrightreg_1_out_6, shiftrightreg_1_out_7, xor_1_out;
  wire [1:0] adder_2_out, multiplexer_4_out, register_1_q, subtractor_1_out;
  wire [6:0] multiplexer_5_out, multiplexer_6_out, multiplexer_8_out, svnsegdec_1_a, svnsegdec_2_a,
       svnsegdec_3_a, svnsegdec_4_a, svnsegdec_5_a;
  wire [7:0] eightbit2compliment_1_o0, eightbit2compliment_2_o0, multiplexer_1_out, multiplexer_3_out;
  wire [15:0] adder_1_out, multiplexer_2_out, preg_1_out_0, shiftleftreg_1_out_0;

  xor xor_1 (xor_1_out, A7, B7);
  eightbit2compliment eightbit2compliment_1 (
    .I7(A7), .I6(A6), .I5(A5), .I4(A4), .I3(A3), .I2(A2), .I1(A1), .I0(A0), .O0(eightbit2compliment_1_o0[0]),
    .O7(eightbit2compliment_1_o0[7]), .O6(eightbit2compliment_1_o0[6]), .O5(eightbit2compliment_1_o0[5]),
    .O4(eightbit2compliment_1_o0[4]), .O3(eightbit2compliment_1_o0[3]), .O2(eightbit2compliment_1_o0[2]),
    .O1(eightbit2compliment_1_o0[1]));
  Adder #(.width(16)) adder_1 (.a(shiftleftreg_1_out_0), .b(preg_1_out_0), .out(adder_1_out));  // open: cin, cout
  Multiplexer #(.width(8)) multiplexer_1 (
    .in0({A7, A6, A5, A4, A3, A2, A1, A0}), .in1(eightbit2compliment_1_o0), .out(multiplexer_1_out), .sel(A7));
  shiftLeftReg shiftleftreg_1 (
    .I_0(multiplexer_1_out[0]), .I_1(multiplexer_1_out[1]), .i_2(multiplexer_1_out[2]),
    .I_3(multiplexer_1_out[3]), .I_4(multiplexer_1_out[4]), .I_5(multiplexer_1_out[5]),
    .I_6(multiplexer_1_out[6]), .i_7(multiplexer_1_out[7]), .Clock(Clk_out), .Enable(controlunit_1_ea),
    .Load(controlunit_1_la), .Out_0(shiftleftreg_1_out_0[0]), .Out_1(shiftleftreg_1_out_0[1]),
    .Out_2(shiftleftreg_1_out_0[2]), .Out_3(shiftleftreg_1_out_0[3]), .Out_4(shiftleftreg_1_out_0[4]),
    .Out_5(shiftleftreg_1_out_0[5]), .Out_6(shiftleftreg_1_out_0[6]), .Out_7(shiftleftreg_1_out_0[7]),
    .Out_8(shiftleftreg_1_out_0[8]), .Out_9(shiftleftreg_1_out_0[9]), .Out_10(shiftleftreg_1_out_0[10]),
    .Out_11(shiftleftreg_1_out_0[11]), .Out_12(shiftleftreg_1_out_0[12]), .Out_13(shiftleftreg_1_out_0[13]),
    .Out_14(shiftleftreg_1_out_0[14]), .Out_15(shiftleftreg_1_out_0[15]));
  Clock #(.highDuration(20), .lowDuration(20)) Clk (.out(Clk_out));
  Multiplexer #(.width(16)) multiplexer_2 (
    .in0({16{1'b0}}), .in1(adder_1_out), .out(multiplexer_2_out), .sel(controlunit_1_psel));
  Button BTNC (.out(BTNC_out));
  PReg preg_1 (
    .I_0(multiplexer_2_out[0]), .I_1(multiplexer_2_out[1]), .I_2(multiplexer_2_out[2]),
    .I_3(multiplexer_2_out[3]), .I_4(multiplexer_2_out[4]), .I_5(multiplexer_2_out[5]),
    .I_6(multiplexer_2_out[6]), .I_7(multiplexer_2_out[7]), .I_8(multiplexer_2_out[8]),
    .I_9(multiplexer_2_out[9]), .I_10(multiplexer_2_out[10]), .I_11(multiplexer_2_out[11]),
    .I_12(multiplexer_2_out[12]), .I_13(multiplexer_2_out[13]), .I_14(multiplexer_2_out[14]),
    .I_15(multiplexer_2_out[15]), .Clock(Clk_out), .Reset(controlunit_1_rstp), .Load(controlunit_1_ep),
    .Out_0(preg_1_out_0[0]), .Out_1(preg_1_out_0[1]), .Out_2(preg_1_out_0[2]), .Out_3(preg_1_out_0[3]),
    .Out_4(preg_1_out_0[4]), .Out_5(preg_1_out_0[5]), .Out_6(preg_1_out_0[6]), .Out_7(preg_1_out_0[7]),
    .Out_8(preg_1_out_0[8]), .Out_9(preg_1_out_0[9]), .Out_10(preg_1_out_0[10]), .Out_11(preg_1_out_0[11]),
    .Out_12(preg_1_out_0[12]), .Out_13(preg_1_out_0[13]), .Out_14(preg_1_out_0[14]), .Out_15(preg_1_out_0[15]));
  shiftRightReg shiftrightreg_1 (
    .i_0(multiplexer_3_out[0]), .I_1(multiplexer_3_out[1]), .I_2(multiplexer_3_out[2]),
    .I_3(multiplexer_3_out[3]), .I_4(multiplexer_3_out[4]), .I_5(multiplexer_3_out[5]),
    .I_6(multiplexer_3_out[6]), .i_7(multiplexer_3_out[7]), .Clock(Clk_out), .Enable(controlunit_1_eb),
    .Load(controlunit_1_lb), .Out_0(shiftrightreg_1_out_0), .Out_1(shiftrightreg_1_out_1),
    .Out_2(shiftrightreg_1_out_2), .Out_3(shiftrightreg_1_out_3), .Out_4(shiftrightreg_1_out_4),
    .Out_5(shiftrightreg_1_out_5), .Out_6(shiftrightreg_1_out_6), .Out_7(shiftrightreg_1_out_7));
  eightbit2compliment eightbit2compliment_2 (
    .I7(B7), .I6(B6), .I5(B5), .I4(B4), .I3(B3), .I2(B2), .I1(B1), .I0(B0), .O0(eightbit2compliment_2_o0[0]),
    .O7(eightbit2compliment_2_o0[7]), .O6(eightbit2compliment_2_o0[6]), .O5(eightbit2compliment_2_o0[5]),
    .O4(eightbit2compliment_2_o0[4]), .O3(eightbit2compliment_2_o0[3]), .O2(eightbit2compliment_2_o0[2]),
    .O1(eightbit2compliment_2_o0[1]));
  nor nor_1 (nor_1_out, shiftrightreg_1_out_7, shiftrightreg_1_out_6, shiftrightreg_1_out_5, shiftrightreg_1_out_4, shiftrightreg_1_out_3, shiftrightreg_1_out_2, shiftrightreg_1_out_1, shiftrightreg_1_out_0);
  LED led_1 (.in(preg_1_out_0[0]));
  LED led_2 (.in(preg_1_out_0[1]));
  LED led_3 (.in(preg_1_out_0[2]));
  LED led_4 (.in(preg_1_out_0[3]));
  LED led_5 (.in(preg_1_out_0[4]));
  LED led_6 (.in(preg_1_out_0[5]));
  LED led_7 (.in(preg_1_out_0[6]));
  LED led_8 (.in(preg_1_out_0[7]));
  LED led_9 (.in(preg_1_out_0[8]));
  LED led_10 (.in(preg_1_out_0[9]));
  LED led_11 (.in(preg_1_out_0[10]));
  LED led_12 (.in(preg_1_out_0[11]));
  LED led_13 (.in(preg_1_out_0[12]));
  LED led_14 (.in(preg_1_out_0[13]));
  LED led_15 (.in(preg_1_out_0[14]));
  LED led_16 (.in(preg_1_out_0[15]));
  LED Out_Sign (.in(xor_1_out));
  ControlUnit controlunit_1 (
    .B0(shiftrightreg_1_out_0), .Z(nor_1_out), .Load(BTNC_out), .Psel(controlunit_1_psel),
    .EP(controlunit_1_ep), .EA(controlunit_1_ea), .EB(controlunit_1_eb), .LA(controlunit_1_la),
    .LB(controlunit_1_lb), .RstP(controlunit_1_rstp));
  Multiplexer #(.width(8)) multiplexer_3 (
    .in0({B7, B6, B5, B4, B3, B2, B1, B0}), .in1(eightbit2compliment_2_o0), .out(multiplexer_3_out), .sel(B7));
  LED Mul_Finished (.in(nor_1_out));
  DoubleDabble doubledabble_1 (
    .A2(preg_1_out_0[2]), .A3(preg_1_out_0[3]), .A4(preg_1_out_0[4]), .A5(preg_1_out_0[5]),
    .A6(preg_1_out_0[6]), .A7(preg_1_out_0[7]), .A8(preg_1_out_0[8]), .A9(preg_1_out_0[9]),
    .A10(preg_1_out_0[10]), .A11(preg_1_out_0[11]), .A12(preg_1_out_0[12]), .A13(preg_1_out_0[13]),
    .A14(preg_1_out_0[14]), .A15(preg_1_out_0[15]), .A0(preg_1_out_0[0]), .A1(preg_1_out_0[1]),
    .Ones2(doubledabble_1_ones2), .ones3(doubledabble_1_ones3), .Tens0(doubledabble_1_tens0),
    .Tens1(doubledabble_1_tens1), .Tens2(doubledabble_1_tens2), .Tens3(doubledabble_1_tens3),
    .hundreds0(doubledabble_1_hundreds0), .hundreds1(doubledabble_1_hundreds1),
    .hundreds2(doubledabble_1_hundreds2), .hundreds3(doubledabble_1_hundreds3),
    .Thousands0(doubledabble_1_thousands0), .Thousands1(doubledabble_1_thousands1),
    .Thousands2(doubledabble_1_thousands2), .Thousands3(doubledabble_1_thousands3),
    .TenThousands0(doubledabble_1_tenthousands0), .TenThousands1(doubledabble_1_tenthousands1),
    .TenThousands2(doubledabble_1_tenthousands2), .TenThousands3(doubledabble_1_tenthousands3),
    .Ones0(doubledabble_1_ones0), .Ones1(doubledabble_1_ones1));
  SvnSegDec svnsegdec_1 (
    .A3(doubledabble_1_ones3), .A2(doubledabble_1_ones2), .A1(doubledabble_1_ones1),
    .A0(doubledabble_1_ones0), .A(svnsegdec_1_a[0]), .B(svnsegdec_1_a[1]), .C(svnsegdec_1_a[2]),
    .D(svnsegdec_1_a[3]), .E(svnsegdec_1_a[4]), .F(svnsegdec_1_a[5]), .G(svnsegdec_1_a[6]));
  SvnSegDec svnsegdec_2 (
    .A3(doubledabble_1_tens3), .A2(doubledabble_1_tens2), .A1(doubledabble_1_tens1),
    .A0(doubledabble_1_tens0), .A(svnsegdec_2_a[0]), .B(svnsegdec_2_a[1]), .C(svnsegdec_2_a[2]),
    .D(svnsegdec_2_a[3]), .E(svnsegdec_2_a[4]), .F(svnsegdec_2_a[5]), .G(svnsegdec_2_a[6]));
  SvnSegDec svnsegdec_3 (
    .A3(doubledabble_1_hundreds3), .A2(doubledabble_1_hundreds2), .A1(doubledabble_1_hundreds1),
    .A0(doubledabble_1_hundreds0), .A(svnsegdec_3_a[0]), .B(svnsegdec_3_a[1]), .C(svnsegdec_3_a[2]),
    .D(svnsegdec_3_a[3]), .E(svnsegdec_3_a[4]), .F(svnsegdec_3_a[5]), .G(svnsegdec_3_a[6]));
  SvnSegDec svnsegdec_4 (
    .A3(doubledabble_1_thousands3), .A2(doubledabble_1_thousands2), .A1(doubledabble_1_thousands1),
    .A0(doubledabble_1_thousands0), .A(svnsegdec_4_a[0]), .B(svnsegdec_4_a[1]), .C(svnsegdec_4_a[2]),
    .D(svnsegdec_4_a[3]), .E(svnsegdec_4_a[4]), .F(svnsegdec_4_a[5]), .G(svnsegdec_4_a[6]));
  SvnSegDec svnsegdec_5 (
    .A3(doubledabble_1_tenthousands3), .A2(doubledabble_1_tenthousands2), .A1(doubledabble_1_tenthousands1),
    .A0(doubledabble_1_tenthousands0), .A(svnsegdec_5_a[0]), .B(svnsegdec_5_a[1]), .C(svnsegdec_5_a[2]),
    .D(svnsegdec_5_a[3]), .E(svnsegdec_5_a[4]), .F(svnsegdec_5_a[5]), .G(svnsegdec_5_a[6]));
  Multiplexer #(.width(2)) multiplexer_4 (
    .in0(adder_2_out), .in1(subtractor_1_out), .out(multiplexer_4_out), .sel(and_2_out));
  Register #(.width(2)) register_1 (
    .D(multiplexer_4_out), .en(or_1_out), .clk(clock_1_out), .Q(register_1_q), .clr(controlunit_1_rstp));
  Clock #(.highDuration(3), .lowDuration(3)) clock_1 (.out(clock_1_out));
  or or_1 (or_1_out, and_2_out, and_1_out);
  Button BTNL (.out(BTNL_out));
  Subtractor #(.width(2)) subtractor_1 (.a(register_1_q), .b(2'b01), .out(subtractor_1_out));  // open: bin, bout
  Adder #(.width(2)) adder_2 (.a(register_1_q), .b(2'b01), .out(adder_2_out));  // open: cin, cout
  Multiplexer #(.select(2), .width(7)) multiplexer_5 (
    .in0(svnsegdec_3_a), .in1(svnsegdec_4_a), .in2(svnsegdec_5_a), .out(multiplexer_5_out), .sel(register_1_q));  // open: in3
  _7_Segment_Display u_7_segment_display_1 (.g(xor_1_out));  // open: f, a, b, e, d, c, dp
  _7_Segment_Display u_7_segment_display_2 (
    .g(multiplexer_5_out[6]), .f(multiplexer_5_out[5]), .a(multiplexer_5_out[0]), .b(multiplexer_5_out[1]),
    .e(multiplexer_5_out[4]), .d(multiplexer_5_out[3]), .c(multiplexer_5_out[2]));  // open: dp
  and and_1 (and_1_out, BTNL_out, multiplexer_7_out);
  Multiplexer #(.select(2), .width(7)) multiplexer_6 (
    .in0(svnsegdec_2_a), .in1(svnsegdec_3_a), .in2(svnsegdec_4_a), .out(multiplexer_6_out), .sel(register_1_q));  // open: in3
  _7_Segment_Display u_7_segment_display_3 (
    .g(multiplexer_6_out[6]), .f(multiplexer_6_out[5]), .a(multiplexer_6_out[0]), .b(multiplexer_6_out[1]),
    .e(multiplexer_6_out[4]), .d(multiplexer_6_out[3]), .c(multiplexer_6_out[2]));  // open: dp
  Multiplexer #(.select(2)) multiplexer_7 (
    .in0(1'b1), .in1(1'b1), .in2(1'b0), .in3(1'b0), .out(multiplexer_7_out), .sel(register_1_q));
  Multiplexer #(.select(2), .width(7)) multiplexer_8 (
    .in0(svnsegdec_1_a), .in1(svnsegdec_2_a), .in2(svnsegdec_3_a), .out(multiplexer_8_out), .sel(register_1_q));  // open: in3
  _7_Segment_Display u_7_segment_display_4 (
    .g(multiplexer_8_out[6]), .f(multiplexer_8_out[5]), .a(multiplexer_8_out[0]), .b(multiplexer_8_out[1]),
    .e(multiplexer_8_out[4]), .d(multiplexer_8_out[3]), .c(multiplexer_8_out[2]));  // open: dp
  Multiplexer #(.select(2)) multiplexer_9 (
    .in0(1'b0), .in1(1'b1), .in2(1'b1), .in3(1'b0), .out(multiplexer_9_out), .sel(register_1_q));
  Button BTNR (.out(BTNR_out));
  and and_2 (and_2_out, multiplexer_9_out, BTNR_out);
endmodule

module eightbit2compliment (
  input  I0,
  input  I1,
  input  I2,
  input  I3,
  input  I4,
  input  I5,
  input  I6,
  input  I7,
  output O0,
  output O1,
  output O2,
  output O3,
  output O4,
  output O5,
  output O6,
  output O7
);

  wire adder_2_cout, adder_3_cout, adder_4_cout, adder_5_cout, adder_6_cout, adder_7_cout, adder_8_cout,
       not_1_out, not_2_out, not_3_out, not_4_out, not_5_out, not_6_out, not_7_out, not_8_out;

  not not_1 (not_1_out, I7);
  not not_2 (not_2_out, I6);
  Adder #(.width(1)) adder_1 (.a(not_1_out), .b(adder_2_cout), .out(O7));  // open: cin, cout
  not not_3 (not_3_out, I5);
  Adder #(.width(1)) adder_2 (.a(not_2_out), .b(adder_3_cout), .out(O6), .cout(adder_2_cout));  // open: cin
  not not_4 (not_4_out, I4);
  Adder #(.width(1)) adder_3 (.a(not_3_out), .b(adder_4_cout), .out(O5), .cout(adder_3_cout));  // open: cin
  Adder #(.width(1)) adder_4 (.a(not_4_out), .b(adder_5_cout), .out(O4), .cout(adder_4_cout));  // open: cin
  not not_5 (not_5_out, I3);
  Adder #(.width(1)) adder_5 (.a(not_5_out), .b(adder_6_cout), .out(O3), .cout(adder_5_cout));  // open: cin
  not not_6 (not_6_out, I2);
  Adder #(.width(1)) adder_6 (.a(not_6_out), .b(adder_7_cout), .out(O2), .cout(adder_6_cout));  // open: cin
  not not_7 (not_7_out, I1);
  Adder #(.width(1)) adder_7 (.a(not_7_out), .b(adder_8_cout), .out(O1), .cout(adder_7_cout));  // open: cin
  not not_8 (not_8_out, I0);
  Adder #(.width(1)) adder_8 (.a(not_8_out), .b(1'b1), .out(O0), .cout(adder_8_cout));  // open: cin
endmodule

// reg
module shiftRightReg (
  input  i_0,
  input  I_1,
  input  I_2,
  input  I_3,
  input  I_4,
  input  I_5,
  input  I_6,
  input  i_7,
  input  Clock,
  input  Enable,
  input  Load,
  output Out_0,
  output Out_1,
  output Out_2,
  output Out_3,
  output Out_4,
  output Out_5,
  output Out_6,
  output Out_7
);

  wire multiplexer_1_out, multiplexer_2_out, multiplexer_3_out, multiplexer_4_out, multiplexer_5_out,
       multiplexer_6_out, multiplexer_7_out, multiplexer_8_out, multiplexer_9_out, multiplexer_10_out,
       multiplexer_11_out, multiplexer_12_out, multiplexer_13_out, multiplexer_14_out, multiplexer_15_out,
       multiplexer_16_out, undriven, undriven_2, undriven_3, undriven_4, undriven_5, undriven_6, undriven_7,
       undriven_8;

  Multiplexer multiplexer_1 (.in0(1'b0), .in1(i_7), .out(multiplexer_1_out), .sel(Load));
  D_Flip_Flop d_ff_1 (.D(multiplexer_2_out), .clk(Clock), .Q(Out_7), .reset(undriven));  // open: Qn, preset
  Multiplexer multiplexer_2 (.in0(Out_7), .in1(multiplexer_1_out), .out(multiplexer_2_out), .sel(Enable));
  Multiplexer multiplexer_3 (.in0(Out_7), .in1(I_6), .out(multiplexer_3_out), .sel(Load));
  D_Flip_Flop d_ff_2 (.D(multiplexer_4_out), .clk(Clock), .Q(Out_6), .reset(undriven_2));  // open: Qn, preset
  Multiplexer multiplexer_4 (.in0(Out_6), .in1(multiplexer_3_out), .out(multiplexer_4_out), .sel(Enable));
  Multiplexer multiplexer_5 (.in0(Out_6), .in1(I_5), .out(multiplexer_5_out), .sel(Load));
  Multiplexer multiplexer_6 (.in0(Out_5), .in1(multiplexer_5_out), .out(multiplexer_6_out), .sel(Enable));
  D_Flip_Flop d_ff_3 (.D(multiplexer_6_out), .clk(Clock), .Q(Out_5), .reset(undriven_3));  // open: Qn, preset
  Multiplexer multiplexer_7 (.in0(Out_5), .in1(I_4), .out(multiplexer_7_out), .sel(Load));
  Multiplexer multiplexer_8 (.in0(Out_4), .in1(multiplexer_7_out), .out(multiplexer_8_out), .sel(Enable));
  D_Flip_Flop d_ff_4 (.D(multiplexer_8_out), .clk(Clock), .Q(Out_4), .reset(undriven_4));  // open: Qn, preset
  Multiplexer multiplexer_9 (.in0(Out_4), .in1(I_3), .out(multiplexer_9_out), .sel(Load));
  Multiplexer multiplexer_10 (.in0(Out_3), .in1(multiplexer_9_out), .out(multiplexer_10_out), .sel(Enable));
  D_Flip_Flop d_ff_5 (.D(multiplexer_10_out), .clk(Clock), .Q(Out_3), .reset(undriven_5));  // open: Qn, preset
  Multiplexer multiplexer_11 (.in0(Out_3), .in1(I_2), .out(multiplexer_11_out), .sel(Load));
  Multiplexer multiplexer_12 (.in0(Out_2), .in1(multiplexer_11_out), .out(multiplexer_12_out), .sel(Enable));
  D_Flip_Flop d_ff_6 (.D(multiplexer_12_out), .clk(Clock), .Q(Out_2), .reset(undriven_6));  // open: Qn, preset
  Multiplexer multiplexer_13 (.in0(Out_2), .in1(I_1), .out(multiplexer_13_out), .sel(Load));
  Multiplexer multiplexer_14 (.in0(Out_1), .in1(multiplexer_13_out), .out(multiplexer_14_out), .sel(Enable));
  D_Flip_Flop d_ff_7 (.D(multiplexer_14_out), .clk(Clock), .Q(Out_1), .reset(undriven_7));  // open: Qn, preset
  Multiplexer multiplexer_15 (.in0(Out_1), .in1(i_0), .out(multiplexer_15_out), .sel(Load));
  Multiplexer multiplexer_16 (.in0(Out_0), .in1(multiplexer_15_out), .out(multiplexer_16_out), .sel(Enable));
  D_Flip_Flop d_ff_8 (.D(multiplexer_16_out), .clk(Clock), .Q(Out_0), .reset(undriven_8));  // open: Qn, preset
endmodule

module shiftLeftReg (
  input  I_0,
  input  I_1,
  input  i_2,
  input  I_3,
  input  I_4,
  input  I_5,
  input  I_6,
  input  i_7,
  input  Clock,
  input  Enable,
  input  Load,
  output Out_0,
  output Out_1,
  output Out_2,
  output Out_3,
  output Out_4,
  output Out_5,
  output Out_6,
  output Out_7,
  output Out_8,
  output Out_9,
  output Out_10,
  output Out_11,
  output Out_12,
  output Out_13,
  output Out_14,
  output Out_15
);

  wire multiplexer_1_out, multiplexer_2_out, multiplexer_3_out, multiplexer_4_out, multiplexer_5_out,
       multiplexer_6_out, multiplexer_7_out, multiplexer_8_out, multiplexer_9_out, multiplexer_10_out,
       multiplexer_11_out, multiplexer_12_out, multiplexer_13_out, multiplexer_14_out, multiplexer_15_out,
       multiplexer_16_out, multiplexer_17_out, multiplexer_18_out, multiplexer_19_out, multiplexer_20_out,
       multiplexer_21_out, multiplexer_22_out, multiplexer_23_out, multiplexer_24_out, multiplexer_25_out,
       multiplexer_26_out, multiplexer_27_out, multiplexer_28_out, multiplexer_29_out, multiplexer_30_out,
       multiplexer_31_out, multiplexer_32_out, undriven, undriven_2, undriven_3, undriven_4, undriven_5,
       undriven_6, undriven_7, undriven_8, undriven_9, undriven_10, undriven_11, undriven_12, undriven_13,
       undriven_14, undriven_15, undriven_16;

  Multiplexer multiplexer_1 (.in0(Out_14), .in1(1'b0), .out(multiplexer_1_out), .sel(Load));
  Multiplexer multiplexer_2 (.in0(Out_6), .in1(i_7), .out(multiplexer_2_out), .sel(Load));
  D_Flip_Flop d_ff_1 (.D(multiplexer_3_out), .clk(Clock), .Q(Out_15), .reset(undriven));  // open: Qn, preset
  Multiplexer multiplexer_3 (.in0(Out_15), .in1(multiplexer_1_out), .out(multiplexer_3_out), .sel(Enable));
  D_Flip_Flop d_ff_2 (.D(multiplexer_4_out), .clk(Clock), .Q(Out_7), .reset(undriven_2));  // open: Qn, preset
  Multiplexer multiplexer_4 (.in0(Out_7), .in1(multiplexer_2_out), .out(multiplexer_4_out), .sel(Enable));
  Multiplexer multiplexer_5 (.in0(Out_13), .in1(1'b0), .out(multiplexer_5_out), .sel(Load));
  Multiplexer multiplexer_6 (.in0(Out_5), .in1(I_6), .out(multiplexer_6_out), .sel(Load));
  D_Flip_Flop d_ff_3 (.D(multiplexer_7_out), .clk(Clock), .Q(Out_14), .reset(undriven_3));  // open: Qn, preset
  Multiplexer multiplexer_7 (.in0(Out_14), .in1(multiplexer_5_out), .out(multiplexer_7_out), .sel(Enable));
  D_Flip_Flop d_ff_4 (.D(multiplexer_8_out), .clk(Clock), .Q(Out_6), .reset(undriven_4));  // open: Qn, preset
  Multiplexer multiplexer_8 (.in0(Out_6), .in1(multiplexer_6_out), .out(multiplexer_8_out), .sel(Enable));
  Multiplexer multiplexer_9 (.in0(Out_12), .in1(1'b0), .out(multiplexer_9_out), .sel(Load));
  Multiplexer multiplexer_10 (.in0(Out_4), .in1(I_5), .out(multiplexer_10_out), .sel(Load));
  Multiplexer multiplexer_11 (.in0(Out_13), .in1(multiplexer_9_out), .out(multiplexer_11_out), .sel(Enable));
  Multiplexer multiplexer_12 (.in0(Out_5), .in1(multiplexer_10_out), .out(multiplexer_12_out), .sel(Enable));
  D_Flip_Flop d_ff_5 (.D(multiplexer_11_out), .clk(Clock), .Q(Out_13), .reset(undriven_5));  // open: Qn, preset
  D_Flip_Flop d_ff_6 (.D(multiplexer_12_out), .clk(Clock), .Q(Out_5), .reset(undriven_6));  // open: Qn, preset
  Multiplexer multiplexer_13 (.in0(Out_11), .in1(1'b0), .out(multiplexer_13_out), .sel(Load));
  Multiplexer multiplexer_14 (.in0(Out_12), .in1(multiplexer_13_out), .out(multiplexer_14_out), .sel(Enable));
  Multiplexer multiplexer_15 (.in0(Out_3), .in1(I_4), .out(multiplexer_15_out), .sel(Load));
  Multiplexer multiplexer_16 (.in0(Out_4), .in1(multiplexer_15_out), .out(multiplexer_16_out), .sel(Enable));
  D_Flip_Flop d_ff_7 (.D(multiplexer_14_out), .clk(Clock), .Q(Out_12), .reset(undriven_7));  // open: Qn, preset
  D_Flip_Flop d_ff_8 (.D(multiplexer_16_out), .clk(Clock), .Q(Out_4), .reset(undriven_8));  // open: Qn, preset
  Multiplexer multiplexer_17 (.in0(Out_10), .in1(1'b0), .out(multiplexer_17_out), .sel(Load));
  Multiplexer multiplexer_18 (.in0(Out_11), .in1(multiplexer_17_out), .out(multiplexer_18_out), .sel(Enable));
  Multiplexer multiplexer_19 (.in0(Out_2), .in1(I_3), .out(multiplexer_19_out), .sel(Load));
  Multiplexer multiplexer_20 (.in0(Out_3), .in1(multiplexer_19_out), .out(multiplexer_20_out), .sel(Enable));
  D_Flip_Flop d_ff_9 (.D(multiplexer_18_out), .clk(Clock), .Q(Out_11), .reset(undriven_9));  // open: Qn, preset
  D_Flip_Flop d_ff_10 (.D(multiplexer_20_out), .clk(Clock), .Q(Out_3), .reset(undriven_10));  // open: Qn, preset
  Multiplexer multiplexer_21 (.in0(Out_9), .in1(1'b0), .out(multiplexer_21_out), .sel(Load));
  Multiplexer multiplexer_22 (.in0(Out_1), .in1(i_2), .out(multiplexer_22_out), .sel(Load));
  Multiplexer multiplexer_23 (.in0(Out_10), .in1(multiplexer_21_out), .out(multiplexer_23_out), .sel(Enable));
  Multiplexer multiplexer_24 (.in0(Out_2), .in1(multiplexer_22_out), .out(multiplexer_24_out), .sel(Enable));
  D_Flip_Flop d_ff_11 (.D(multiplexer_23_out), .clk(Clock), .Q(Out_10), .reset(undriven_11));  // open: Qn, preset
  D_Flip_Flop d_ff_12 (.D(multiplexer_24_out), .clk(Clock), .Q(Out_2), .reset(undriven_12));  // open: Qn, preset
  Multiplexer multiplexer_25 (.in0(Out_8), .in1(1'b0), .out(multiplexer_25_out), .sel(Load));
  Multiplexer multiplexer_26 (.in0(Out_9), .in1(multiplexer_25_out), .out(multiplexer_26_out), .sel(Enable));
  Multiplexer multiplexer_27 (.in0(Out_0), .in1(I_1), .out(multiplexer_27_out), .sel(Load));
  Multiplexer multiplexer_28 (.in0(Out_1), .in1(multiplexer_27_out), .out(multiplexer_28_out), .sel(Enable));
  D_Flip_Flop d_ff_13 (.D(multiplexer_26_out), .clk(Clock), .Q(Out_9), .reset(undriven_13));  // open: Qn, preset
  D_Flip_Flop d_ff_14 (.D(multiplexer_28_out), .clk(Clock), .Q(Out_1), .reset(undriven_14));  // open: Qn, preset
  Multiplexer multiplexer_29 (.in0(Out_7), .in1(1'b0), .out(multiplexer_29_out), .sel(Load));
  Multiplexer multiplexer_30 (.in0(1'b0), .in1(I_0), .out(multiplexer_30_out), .sel(Load));
  Multiplexer multiplexer_31 (.in0(Out_8), .in1(multiplexer_29_out), .out(multiplexer_31_out), .sel(Enable));
  Multiplexer multiplexer_32 (.in0(Out_0), .in1(multiplexer_30_out), .out(multiplexer_32_out), .sel(Enable));
  D_Flip_Flop d_ff_15 (.D(multiplexer_31_out), .clk(Clock), .Q(Out_8), .reset(undriven_15));  // open: Qn, preset
  D_Flip_Flop d_ff_16 (.D(multiplexer_32_out), .clk(Clock), .Q(Out_0), .reset(undriven_16));  // open: Qn, preset
endmodule

module ControlUnit (
  input  B0,
  input  Z,
  input  Load,
  output Psel,
  output EP,
  output EA,
  output EB,
  output LA,
  output LB,
  output RstP
);

  wire not_1_out, not_2_out;

  not not_1 (not_1_out, Z);
  or or_1 (EA, not_1_out, Load);
  not not_2 (not_2_out, Load);
  and and_1 (EP, B0, not_2_out);

  assign EB = EA;
  assign LA = Load;
  assign LB = Load;
  assign Psel = B0;
  assign RstP = Load;
endmodule

module SvnSegDec (
  input  A3,
  input  A2,
  input  A1,
  input  A0,
  output A,
  output B,
  output C,
  output D,
  output E,
  output F,
  output G
);

  wire and_1_out, and_2_out, and_3_out, and_4_out, and_5_out, and_6_out, and_7_out, and_8_out, and_9_out,
       and_10_out, and_11_out, and_12_out, and_13_out, and_14_out, and_15_out, and_16_out, and_17_out,
       not_1_out, not_2_out, not_3_out, not_4_out, or_1_out, or_2_out, or_3_out, or_4_out, or_5_out,
       or_6_out, or_7_out, or_8_out, or_10_out, or_14_out, or_15_out;

  not not_1 (not_1_out, A2);
  not not_2 (not_2_out, A3);
  not not_3 (not_3_out, A1);
  not not_4 (not_4_out, A0);
  and and_1 (and_1_out, not_1_out, not_4_out);
  and and_2 (and_2_out, A2, A0);
  and and_3 (and_3_out, not_3_out, not_4_out);
  or or_1 (or_1_out, not_3_out, A0);
  and and_4 (and_4_out, not_1_out, not_4_out);
  and and_5 (and_5_out, not_1_out, A1);
  and and_6 (and_6_out, A2, not_3_out);
  and and_7 (and_7_out, not_3_out, not_4_out);
  and and_8 (and_8_out, A2, not_3_out);
  and and_9 (and_9_out, A2, not_4_out);
  and and_10 (and_10_out, not_1_out, A1);
  and and_11 (and_11_out, A2, not_3_out);
  and and_12 (and_12_out, A2, not_4_out);
  and and_13 (and_13_out, not_1_out, not_4_out);
  and and_14 (and_14_out, A1, not_4_out);
  or or_2 (or_2_out, and_7_out, and_8_out);
  or or_3 (or_3_out, and_9_out, A3);
  or or_4 (or_4_out, and_10_out, and_11_out);
  or or_5 (or_5_out, and_12_out, A3);
  or or_6 (or_6_out, and_1_out, A1);
  or or_7 (or_7_out, and_2_out, A3);
  or or_8 (or_8_out, not_1_out, and_3_out);
  and and_15 (and_15_out, A1, A0);
  or or_9 (C, or_1_out, A2);
  or or_10 (or_10_out, and_4_out, and_5_out);
  and and_16 (and_16_out, A1, not_4_out);
  and and_17 (and_17_out, and_6_out, A0);
  or or_11 (E, and_13_out, and_14_out);
  or or_12 (A, or_6_out, or_7_out);
  or or_13 (B, or_8_out, and_15_out);
  or or_14 (or_14_out, or_10_out, and_16_out);
  or or_15 (or_15_out, and_17_out, A3);
  or or_16 (F, or_2_out, or_3_out);
  or or_17 (G, or_4_out, or_5_out);
  or or_18 (D, or_14_out, or_15_out);
endmodule

module ConditionalAdder (
  input  A3,
  input  A2,
  input  A1,
  input  A0,
  output O3,
  output O2,
  output O1,
  output O0
);

  wire adder_1_cout, and_1_out, and_2_out, and_3_out, not_1_out, or_1_out, or_2_out, xor_2_out;

  or or_1 (or_1_out, A1, A0);
  and and_1 (and_1_out, A2, or_1_out);
  or or_2 (or_2_out, A3, and_1_out);
  not not_1 (not_1_out, A1);
  xor xor_1 (O0, or_2_out, A0);
  and and_2 (and_2_out, or_2_out, O0);
  and and_3 (and_3_out, not_1_out, and_2_out);
  xor xor_2 (xor_2_out, or_2_out, and_3_out);
  Adder #(.width(1)) adder_1 (.a(A2), .b(xor_2_out), .out(O2), .cout(adder_1_cout));  // open: cin
  xor xor_3 (O1, A1, and_2_out);
  xor xor_4 (O3, A3, adder_1_cout);
endmodule

module DoubleDabble (
  input  A0,
  input  A1,
  input  A2,
  input  A3,
  input  A4,
  input  A5,
  input  A6,
  input  A7,
  input  A8,
  input  A9,
  input  A10,
  input  A11,
  input  A12,
  input  A13,
  input  A14,
  input  A15,
  output Ones0,
  output Ones1,
  output Ones2,
  output ones3,
  output Tens0,
  output Tens1,
  output Tens2,
  output Tens3,
  output hundreds0,
  output hundreds1,
  output hundreds2,
  output hundreds3,
  output Thousands0,
  output Thousands1,
  output Thousands2,
  output Thousands3,
  output TenThousands0,
  output TenThousands1,
  output TenThousands2,
  output TenThousands3
);

  wire conditionaladder_1_o0, conditionaladder_1_o1, conditionaladder_1_o2, conditionaladder_1_o3,
       conditionaladder_2_o0, conditionaladder_2_o1, conditionaladder_2_o2, conditionaladder_2_o3,
       conditionaladder_3_o0, conditionaladder_3_o1, conditionaladder_3_o2, conditionaladder_3_o3,
       conditionaladder_4_o0, conditionaladder_4_o1, conditionaladder_4_o2, conditionaladder_4_o3,
       conditionaladder_5_o0, conditionaladder_5_o1, conditionaladder_5_o2, conditionaladder_5_o3,
       conditionaladder_6_o0, conditionaladder_6_o1, conditionaladder_6_o2, conditionaladder_6_o3,
       conditionaladder_7_o0, conditionaladder_7_o1, conditionaladder_7_o2, conditionaladder_7_o3,
       conditionaladder_8_o0, conditionaladder_8_o1, conditionaladder_8_o2, conditionaladder_8_o3,
       conditionaladder_9_o0, conditionaladder_9_o1, conditionaladder_9_o2, conditionaladder_9_o3,
       conditionaladder_10_o0, conditionaladder_10_o1, conditionaladder_10_o2, conditionaladder_10_o3,
       conditionaladder_11_o0, conditionaladder_11_o1, conditionaladder_11_o2, conditionaladder_11_o3,
       conditionaladder_12_o0, conditionaladder_12_o1, conditionaladder_12_o2, conditionaladder_12_o3,
       conditionaladder_13_o0, conditionaladder_13_o1, conditionaladder_13_o2, conditionaladder_13_o3,
       conditionaladder_14_o0, conditionaladder_14_o1, conditionaladder_14_o2, conditionaladder_14_o3,
       conditionaladder_15_o0, conditionaladder_15_o1, conditionaladder_15_o2, conditionaladder_15_o3,
       conditionaladder_16_o0, conditionaladder_16_o1, conditionaladder_16_o2, conditionaladder_16_o3,
       conditionaladder_17_o0, conditionaladder_17_o1, conditionaladder_17_o2, conditionaladder_17_o3,
       conditionaladder_18_o0, conditionaladder_18_o1, conditionaladder_18_o2, conditionaladder_18_o3,
       conditionaladder_19_o0, conditionaladder_19_o1, conditionaladder_19_o2, conditionaladder_19_o3,
       conditionaladder_20_o0, conditionaladder_20_o1, conditionaladder_20_o2, conditionaladder_20_o3,
       conditionaladder_21_o0, conditionaladder_21_o1, conditionaladder_21_o2, conditionaladder_21_o3,
       conditionaladder_22_o0, conditionaladder_22_o1, conditionaladder_22_o2, conditionaladder_22_o3,
       conditionaladder_23_o0, conditionaladder_23_o1, conditionaladder_23_o2, conditionaladder_23_o3,
       conditionaladder_24_o0, conditionaladder_24_o1, conditionaladder_24_o2, conditionaladder_24_o3,
       conditionaladder_25_o0, conditionaladder_25_o1, conditionaladder_25_o2, conditionaladder_25_o3,
       conditionaladder_26_o0, conditionaladder_26_o1, conditionaladder_26_o2, conditionaladder_26_o3,
       conditionaladder_27_o0, conditionaladder_27_o1, conditionaladder_27_o2, conditionaladder_27_o3,
       conditionaladder_28_o0, conditionaladder_28_o1, conditionaladder_28_o2, conditionaladder_28_o3,
       conditionaladder_29_o0, conditionaladder_29_o1, conditionaladder_29_o2, conditionaladder_29_o3,
       conditionaladder_30_o0, conditionaladder_30_o1, conditionaladder_30_o2, conditionaladder_30_o3,
       conditionaladder_35_o3;

  ConditionalAdder conditionaladder_1 (
    .A3(1'b0), .A2(A15), .A1(A14), .A0(A13), .O1(conditionaladder_1_o1), .O0(conditionaladder_1_o0),
    .O3(conditionaladder_1_o3), .O2(conditionaladder_1_o2));
  ConditionalAdder conditionaladder_2 (
    .A3(conditionaladder_1_o2), .A2(conditionaladder_1_o1), .A1(conditionaladder_1_o0), .A0(A12),
    .O1(conditionaladder_2_o1), .O0(conditionaladder_2_o0), .O3(conditionaladder_2_o3),
    .O2(conditionaladder_2_o2));
  ConditionalAdder conditionaladder_3 (
    .A3(conditionaladder_2_o2), .A2(conditionaladder_2_o1), .A1(conditionaladder_2_o0), .A0(A11),
    .O1(conditionaladder_3_o1), .O0(conditionaladder_3_o0), .O3(conditionaladder_3_o3),
    .O2(conditionaladder_3_o2));
  ConditionalAdder conditionaladder_4 (
    .A3(conditionaladder_3_o2), .A2(conditionaladder_3_o1), .A1(conditionaladder_3_o0), .A0(A10),
    .O1(conditionaladder_4_o1), .O0(conditionaladder_4_o0), .O3(conditionaladder_4_o3),
    .O2(conditionaladder_4_o2));
  ConditionalAdder conditionaladder_5 (
    .A3(1'b0), .A2(conditionaladder_1_o3), .A1(conditionaladder_2_o3), .A0(conditionaladder_3_o3),
    .O1(conditionaladder_5_o1), .O0(conditionaladder_5_o0), .O3(conditionaladder_5_o3),
    .O2(conditionaladder_5_o2));
  ConditionalAdder conditionaladder_6 (
    .A3(conditionaladder_4_o2), .A2(conditionaladder_4_o1), .A1(conditionaladder_4_o0), .A0(A9),
    .O1(conditionaladder_6_o1), .O0(conditionaladder_6_o0), .O3(conditionaladder_6_o3),
    .O2(conditionaladder_6_o2));
  ConditionalAdder conditionaladder_7 (
    .A3(conditionaladder_5_o2), .A2(conditionaladder_5_o1), .A1(conditionaladder_5_o0),
    .A0(conditionaladder_4_o3), .O1(conditionaladder_7_o1), .O0(conditionaladder_7_o0),
    .O3(conditionaladder_7_o3), .O2(conditionaladder_7_o2));
  ConditionalAdder conditionaladder_8 (
    .A3(conditionaladder_6_o2), .A2(conditionaladder_6_o1), .A1(conditionaladder_6_o0), .A0(A8),
    .O1(conditionaladder_8_o1), .O0(conditionaladder_8_o0), .O3(conditionaladder_8_o3),
    .O2(conditionaladder_8_o2));
  ConditionalAdder conditionaladder_9 (
    .A3(conditionaladder_7_o2), .A2(conditionaladder_7_o1), .A1(conditionaladder_7_o0),
    .A0(conditionaladder_6_o3), .O1(conditionaladder_9_o1), .O0(conditionaladder_9_o0),
    .O3(conditionaladder_9_o3), .O2(conditionaladder_9_o2));
  ConditionalAdder conditionaladder_10 (
    .A3(conditionaladder_8_o2), .A2(conditionaladder_8_o1), .A1(conditionaladder_8_o0), .A0(A7),
    .O1(conditionaladder_10_o1), .O0(conditionaladder_10_o0), .O3(conditionaladder_10_o3),
    .O2(conditionaladder_10_o2));
  ConditionalAdder conditionaladder_11 (
    .A3(conditionaladder_9_o2), .A2(conditionaladder_9_o1), .A1(conditionaladder_9_o0),
    .A0(conditionaladder_8_o3), .O1(conditionaladder_11_o1), .O0(conditionaladder_11_o0),
    .O3(conditionaladder_11_o3), .O2(conditionaladder_11_o2));
  ConditionalAdder conditionaladder_12 (
    .A3(1'b0), .A2(conditionaladder_5_o3), .A1(conditionaladder_7_o3), .A0(conditionaladder_9_o3),
    .O1(conditionaladder_12_o1), .O0(conditionaladder_12_o0), .O3(conditionaladder_12_o3),
    .O2(conditionaladder_12_o2));
  ConditionalAdder conditionaladder_13 (
    .A3(conditionaladder_10_o2), .A2(conditionaladder_10_o1), .A1(conditionaladder_10_o0), .A0(A6),
    .O1(conditionaladder_13_o1), .O0(conditionaladder_13_o0), .O3(conditionaladder_13_o3),
    .O2(conditionaladder_13_o2));
  ConditionalAdder conditionaladder_14 (
    .A3(conditionaladder_11_o2), .A2(conditionaladder_11_o1), .A1(conditionaladder_11_o0),
    .A0(conditionaladder_10_o3), .O1(conditionaladder_14_o1), .O0(conditionaladder_14_o0),
    .O3(conditionaladder_14_o3), .O2(conditionaladder_14_o2));
  ConditionalAdder conditionaladder_15 (
    .A3(conditionaladder_12_o2), .A2(conditionaladder_12_o1), .A1(conditionaladder_12_o0),
    .A0(conditionaladder_11_o3), .O1(conditionaladder_15_o1), .O0(conditionaladder_15_o0),
    .O3(conditionaladder_15_o3), .O2(conditionaladder_15_o2));
  ConditionalAdder conditionaladder_16 (
    .A3(conditionaladder_13_o2), .A2(conditionaladder_13_o1), .A1(conditionaladder_13_o0), .A0(A5),
    .O1(conditionaladder_16_o1), .O0(conditionaladder_16_o0), .O3(conditionaladder_16_o3),
    .O2(conditionaladder_16_o2));
  ConditionalAdder conditionaladder_17 (
    .A3(conditionaladder_14_o2), .A2(conditionaladder_14_o1), .A1(conditionaladder_14_o0),
    .A0(conditionaladder_13_o3), .O1(conditionaladder_17_o1), .O0(conditionaladder_17_o0),
    .O3(conditionaladder_17_o3), .O2(conditionaladder_17_o2));
  ConditionalAdder conditionaladder_18 (
    .A3(conditionaladder_15_o2), .A2(conditionaladder_15_o1), .A1(conditionaladder_15_o0),
    .A0(conditionaladder_14_o3), .O1(conditionaladder_18_o1), .O0(conditionaladder_18_o0),
    .O3(conditionaladder_18_o3), .O2(conditionaladder_18_o2));
  ConditionalAdder conditionaladder_19 (
    .A3(conditionaladder_16_o2), .A2(conditionaladder_16_o1), .A1(conditionaladder_16_o0), .A0(A4),
    .O1(conditionaladder_19_o1), .O0(conditionaladder_19_o0), .O3(conditionaladder_19_o3),
    .O2(conditionaladder_19_o2));
  ConditionalAdder conditionaladder_20 (
    .A3(conditionaladder_17_o2), .A2(conditionaladder_17_o1), .A1(conditionaladder_17_o0),
    .A0(conditionaladder_16_o3), .O1(conditionaladder_20_o1), .O0(conditionaladder_20_o0),
    .O3(conditionaladder_20_o3), .O2(conditionaladder_20_o2));
  ConditionalAdder conditionaladder_21 (
    .A3(conditionaladder_18_o2), .A2(conditionaladder_18_o1), .A1(conditionaladder_18_o0),
    .A0(conditionaladder_17_o3), .O1(conditionaladder_21_o1), .O0(conditionaladder_21_o0),
    .O3(conditionaladder_21_o3), .O2(conditionaladder_21_o2));
  ConditionalAdder conditionaladder_22 (
    .A3(1'b0), .A2(conditionaladder_12_o3), .A1(conditionaladder_15_o3), .A0(conditionaladder_18_o3),
    .O1(conditionaladder_22_o1), .O0(conditionaladder_22_o0), .O3(conditionaladder_22_o3),
    .O2(conditionaladder_22_o2));
  ConditionalAdder conditionaladder_23 (
    .A3(conditionaladder_19_o2), .A2(conditionaladder_19_o1), .A1(conditionaladder_19_o0), .A0(A3),
    .O1(conditionaladder_23_o1), .O0(conditionaladder_23_o0), .O3(conditionaladder_23_o3),
    .O2(conditionaladder_23_o2));
  ConditionalAdder conditionaladder_24 (
    .A3(conditionaladder_20_o2), .A2(conditionaladder_20_o1), .A1(conditionaladder_20_o0),
    .A0(conditionaladder_19_o3), .O1(conditionaladder_24_o1), .O0(conditionaladder_24_o0),
    .O3(conditionaladder_24_o3), .O2(conditionaladder_24_o2));
  ConditionalAdder conditionaladder_25 (
    .A3(conditionaladder_21_o2), .A2(conditionaladder_21_o1), .A1(conditionaladder_21_o0),
    .A0(conditionaladder_20_o3), .O1(conditionaladder_25_o1), .O0(conditionaladder_25_o0),
    .O3(conditionaladder_25_o3), .O2(conditionaladder_25_o2));
  ConditionalAdder conditionaladder_26 (
    .A3(conditionaladder_22_o2), .A2(conditionaladder_22_o1), .A1(conditionaladder_22_o0),
    .A0(conditionaladder_21_o3), .O1(conditionaladder_26_o1), .O0(conditionaladder_26_o0),
    .O3(conditionaladder_26_o3), .O2(conditionaladder_26_o2));
  ConditionalAdder conditionaladder_27 (
    .A3(conditionaladder_23_o2), .A2(conditionaladder_23_o1), .A1(conditionaladder_23_o0), .A0(A2),
    .O1(conditionaladder_27_o1), .O0(conditionaladder_27_o0), .O3(conditionaladder_27_o3),
    .O2(conditionaladder_27_o2));
  ConditionalAdder conditionaladder_28 (
    .A3(conditionaladder_24_o2), .A2(conditionaladder_24_o1), .A1(conditionaladder_24_o0),
    .A0(conditionaladder_23_o3), .O1(conditionaladder_28_o1), .O0(conditionaladder_28_o0),
    .O3(conditionaladder_28_o3), .O2(conditionaladder_28_o2));
  ConditionalAdder conditionaladder_29 (
    .A3(conditionaladder_25_o2), .A2(conditionaladder_25_o1), .A1(conditionaladder_25_o0),
    .A0(conditionaladder_24_o3), .O1(conditionaladder_29_o1), .O0(conditionaladder_29_o0),
    .O3(conditionaladder_29_o3), .O2(conditionaladder_29_o2));
  ConditionalAdder conditionaladder_30 (
    .A3(conditionaladder_26_o2), .A2(conditionaladder_26_o1), .A1(conditionaladder_26_o0),
    .A0(conditionaladder_25_o3), .O1(conditionaladder_30_o1), .O0(conditionaladder_30_o0),
    .O3(conditionaladder_30_o3), .O2(conditionaladder_30_o2));
  ConditionalAdder conditionaladder_31 (
    .A3(conditionaladder_27_o2), .A2(conditionaladder_27_o1), .A1(conditionaladder_27_o0), .A0(A1),
    .O1(Ones2), .O0(Ones1), .O3(Tens0), .O2(ones3));
  ConditionalAdder conditionaladder_32 (
    .A3(conditionaladder_28_o2), .A2(conditionaladder_28_o1), .A1(conditionaladder_28_o0),
    .A0(conditionaladder_27_o3), .O1(Tens2), .O0(Tens1), .O3(hundreds0), .O2(Tens3));
  ConditionalAdder conditionaladder_33 (
    .A3(conditionaladder_29_o2), .A2(conditionaladder_29_o1), .A1(conditionaladder_29_o0),
    .A0(conditionaladder_28_o3), .O1(hundreds2), .O0(hundreds1), .O3(Thousands0), .O2(hundreds3));
  ConditionalAdder conditionaladder_34 (
    .A3(conditionaladder_30_o2), .A2(conditionaladder_30_o1), .A1(conditionaladder_30_o0),
    .A0(conditionaladder_29_o3), .O1(Thousands2), .O0(Thousands1), .O3(TenThousands0), .O2(Thousands3));
  ConditionalAdder conditionaladder_35 (
    .A3(1'b0), .A2(conditionaladder_22_o3), .A1(conditionaladder_26_o3), .A0(conditionaladder_30_o3),
    .O1(TenThousands2), .O0(TenThousands1), .O3(conditionaladder_35_o3), .O2(TenThousands3));

  assign Ones0 = A0;
endmodule

module UniversalReg (
  input  S1,
  input  S0,
  input  A4,
  input  A3,
  input  A2,
  input  A1,
  input  Test12,
  input  A0,
  input  Test13,
  output O6,
  output O5,
  output O4,
  output O3,
  output O2,
  output O1,
  output O0
);

  wire clock_1_out, clock_2_out, clock_3_out, clock_4_out, clock_5_out, clock_6_out, clock_7_out,
       multiplexer_1_out, multiplexer_2_out, multiplexer_3_out, multiplexer_4_out, multiplexer_5_out,
       multiplexer_6_out, multiplexer_7_out;

  Multiplexer #(.select(2)) multiplexer_1 (
    .in0(A4), .in1(O0), .in2(O5), .in3(O6), .out(multiplexer_1_out), .sel({S0, S1}));
  D_Flip_Flop d_ff_1 (.D(multiplexer_1_out), .clk(clock_1_out), .Q(O6));  // open: Qn, preset, reset
  Clock clock_1 (.out(clock_1_out));
  D_Flip_Flop d_ff_2 (.D(multiplexer_2_out), .clk(clock_2_out), .Q(O5));  // open: Qn, preset, reset
  Clock clock_2 (.out(clock_2_out));
  Multiplexer #(.select(2)) multiplexer_2 (
    .in0(A3), .in1(O6), .in2(O4), .in3(O5), .out(multiplexer_2_out), .sel({S0, S1}));
  Clock clock_3 (.out(clock_3_out));
  Multiplexer #(.select(2)) multiplexer_3 (
    .in0(A2), .in1(O5), .in2(O3), .in3(O4), .out(multiplexer_3_out), .sel({S0, S1}));
  D_Flip_Flop d_ff_3 (.D(multiplexer_3_out), .clk(clock_3_out), .Q(O4));  // open: Qn, preset, reset
  Multiplexer #(.select(2)) multiplexer_4 (
    .in0(A1), .in1(O4), .in2(O2), .in3(O3), .out(multiplexer_4_out), .sel({S0, S1}));
  D_Flip_Flop d_ff_4 (.D(multiplexer_4_out), .clk(clock_4_out), .Q(O3));  // open: Qn, preset, reset
  Clock clock_4 (.out(clock_4_out));
  D_Flip_Flop d_ff_5 (.D(multiplexer_5_out), .clk(clock_5_out), .Q(O2));  // open: Qn, preset, reset
  Clock clock_5 (.out(clock_5_out));
  Multiplexer #(.select(2)) multiplexer_5 (
    .in0(A0), .in1(O3), .in2(O1), .in3(O2), .out(multiplexer_5_out), .sel({S0, S1}));
  Multiplexer #(.select(2)) multiplexer_6 (
    .in0(Test12), .in1(O2), .in2(O0), .in3(O1), .out(multiplexer_6_out), .sel({S0, S1}));
  D_Flip_Flop d_ff_6 (.D(multiplexer_6_out), .clk(clock_6_out), .Q(O1));  // open: Qn, preset, reset
  Clock clock_6 (.out(clock_6_out));
  D_Flip_Flop d_ff_7 (.D(multiplexer_7_out), .clk(clock_7_out), .Q(O0));  // open: Qn, preset, reset
  Clock clock_7 (.out(clock_7_out));
  Multiplexer #(.select(2)) multiplexer_7 (
    .in0(Test13), .in1(O1), .in2(O6), .in3(O0), .out(multiplexer_7_out), .sel({S0, S1}));
endmodule

module PReg (
  input  I_0,
  input  I_1,
  input  I_2,
  input  I_3,
  input  I_4,
  input  I_5,
  input  I_6,
  input  I_7,
  input  I_8,
  input  I_9,
  input  I_10,
  input  I_11,
  input  I_12,
  input  I_13,
  input  I_14,
  input  I_15,
  input  Clock,
  input  Reset,
  input  Load,
  output Out_0,
  output Out_1,
  output Out_2,
  output Out_3,
  output Out_4,
  output Out_5,
  output Out_6,
  output Out_7,
  output Out_8,
  output Out_9,
  output Out_10,
  output Out_11,
  output Out_12,
  output Out_13,
  output Out_14,
  output Out_15
);

  wire multiplexer_1_out, multiplexer_2_out, multiplexer_3_out, multiplexer_4_out, multiplexer_5_out,
       multiplexer_6_out, multiplexer_7_out, multiplexer_8_out, multiplexer_9_out, multiplexer_10_out,
       multiplexer_11_out, multiplexer_12_out, multiplexer_13_out, multiplexer_14_out, multiplexer_15_out,
       multiplexer_16_out;

  Multiplexer multiplexer_1 (.in0(Out_2), .in1(I_2), .out(multiplexer_1_out), .sel(Load));
  Multiplexer multiplexer_2 (.in0(Out_3), .in1(I_3), .out(multiplexer_2_out), .sel(Load));
  Multiplexer multiplexer_3 (.in0(Out_4), .in1(I_4), .out(multiplexer_3_out), .sel(Load));
  Multiplexer multiplexer_4 (.in0(Out_5), .in1(I_5), .out(multiplexer_4_out), .sel(Load));
  Multiplexer multiplexer_5 (.in0(Out_6), .in1(I_6), .out(multiplexer_5_out), .sel(Load));
  Multiplexer multiplexer_6 (.in0(Out_7), .in1(I_7), .out(multiplexer_6_out), .sel(Load));
  Multiplexer multiplexer_7 (.in0(Out_8), .in1(I_8), .out(multiplexer_7_out), .sel(Load));
  Multiplexer multiplexer_8 (.in0(Out_9), .in1(I_9), .out(multiplexer_8_out), .sel(Load));
  Multiplexer multiplexer_9 (.in0(Out_10), .in1(I_10), .out(multiplexer_9_out), .sel(Load));
  Multiplexer multiplexer_10 (.in0(Out_11), .in1(I_11), .out(multiplexer_10_out), .sel(Load));
  Multiplexer multiplexer_11 (.in0(Out_12), .in1(I_12), .out(multiplexer_11_out), .sel(Load));
  Multiplexer multiplexer_12 (.in0(Out_13), .in1(I_13), .out(multiplexer_12_out), .sel(Load));
  Multiplexer multiplexer_13 (.in0(Out_14), .in1(I_14), .out(multiplexer_13_out), .sel(Load));
  Multiplexer multiplexer_14 (.in0(Out_15), .in1(I_15), .out(multiplexer_14_out), .sel(Load));
  Multiplexer multiplexer_15 (.in0(Out_0), .in1(I_0), .out(multiplexer_15_out), .sel(Load));
  D_Flip_Flop d_ff_1 (.D(multiplexer_15_out), .clk(Clock), .Q(Out_0), .reset(Reset));  // open: Qn, preset
  Multiplexer multiplexer_16 (.in0(Out_1), .in1(I_1), .out(multiplexer_16_out), .sel(Load));
  D_Flip_Flop d_ff_2 (.D(multiplexer_16_out), .clk(Clock), .Q(Out_1), .reset(Reset));  // open: Qn, preset
  D_Flip_Flop d_ff_3 (.D(multiplexer_1_out), .clk(Clock), .Q(Out_2), .reset(Reset));  // open: Qn, preset
  D_Flip_Flop d_ff_4 (.D(multiplexer_2_out), .clk(Clock), .Q(Out_3), .reset(Reset));  // open: Qn, preset
  D_Flip_Flop d_ff_5 (.D(multiplexer_3_out), .clk(Clock), .Q(Out_4), .reset(Reset));  // open: Qn, preset
  D_Flip_Flop d_ff_6 (.D(multiplexer_4_out), .clk(Clock), .Q(Out_5), .reset(Reset));  // open: Qn, preset
  D_Flip_Flop d_ff_7 (.D(multiplexer_5_out), .clk(Clock), .Q(Out_6), .reset(Reset));  // open: Qn, preset
  D_Flip_Flop d_ff_8 (.D(multiplexer_6_out), .clk(Clock), .Q(Out_7), .reset(Reset));  // open: Qn, preset
  D_Flip_Flop d_ff_9 (.D(multiplexer_7_out), .clk(Clock), .Q(Out_8), .reset(Reset));  // open: Qn, preset
  D_Flip_Flop d_ff_10 (.D(multiplexer_8_out), .clk(Clock), .Q(Out_9), .reset(Reset));  // open: Qn, preset
  D_Flip_Flop d_ff_11 (.D(multiplexer_9_out), .clk(Clock), .Q(Out_10), .reset(Reset));  // open: Qn, preset
  D_Flip_Flop d_ff_12 (.D(multiplexer_10_out), .clk(Clock), .Q(Out_11), .reset(Reset));  // open: Qn, preset
  D_Flip_Flop d_ff_13 (.D(multiplexer_11_out), .clk(Clock), .Q(Out_12), .reset(Reset));  // open: Qn, preset
  D_Flip_Flop d_ff_14 (.D(multiplexer_12_out), .clk(Clock), .Q(Out_13), .reset(Reset));  // open: Qn, preset
  D_Flip_Flop d_ff_15 (.D(multiplexer_13_out), .clk(Clock), .Q(Out_14), .reset(Reset));  // open: Qn, preset
  D_Flip_Flop d_ff_16 (.D(multiplexer_14_out), .clk(Clock), .Q(Out_15), .reset(Reset));  // open: Qn, preset
endmodule
